# Fritzing sketch esp_sparsnas_gateway_MCUv3_version2 (saved by Fritzing 0.9.3b)
breadboards: 1

parts:
  Part1 = Adafruit RFM69HCW Transceiver Radio [part_number="Adafruit #3070 and #3071"]
  U1 = NodeMCU V3.0
  J1 = Power Jack [package=power_jack_pth_lock]
  C2 = Ceramic Capacitor [capacitance=100nF package="100 mil [THT, multilayer]"]
  C1 = Tantalum Capacitor [capacitance=0.47mF package="100 mil [THT, tantalum]"]
  L1 = Inductor [inductance=100µH package="400 mil [THT]"]

nets:
  N1: Part1.VIN, L1.pin_1
  GND: Part1.GND, U1.GND, J1.GND, C2.0, C1.-
  N2: Part1.DIO0, U1.D1
  N3: Part1.SCK, U1.D5
  N4: Part1.MISO, U1.D6
  N5: Part1.MOSI, U1.D7
  N6: Part1.CS, U1.D8
  N7: U1.3V3, L1.pin_0
  N8: U1.Vin, J1.PWR, C2.1, C1.+

custom parts:
  Adafruit RFM69HCW Transceiver Radio: Sending data over long distances is like magic, and now you can be a magician with this range of powerful and easy-to-use radio modules. Sure, sometimes you want to talk to a computer (a good time to use WiFi) or perhaps communicate with a Phone (choose Bluetooth Low Energy!) but what if you want to send data very far? Most WiFi, Bluetooth, Zigbee and other wireless chipsets use 2.4GHz, which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
  NodeMCU V3.0: ESP8266 based NodeMCU
